// Logisim project 16bit CpU.circ as structural Verilog: 5 circuits, main circuit main
module main (
  input  [3:0] in_1,
  input  [3:0] in_2,
  input  in_3,
  input  [3:0] in_4,
  input  [15:0] in_5,
  input  [2:0] in_6,
  input  [15:0] in_7,
  input  [2:0] in_8,
  input  in_9,
  output [3:0] out_10,
  output [15:0] out_11,
  output [15:0] out_12,
  output [2:0] out_13,
  output [2:0] out_14,
  output [5:0] out_15
);

  wire alu_1_out_9, and_1_out, clock_1_out, control_unit_1_alusource, control_unit_1_branch,
       control_unit_1_jump, control_unit_1_mem_read, control_unit_1_mem_write, control_unit_1_memtoreg,
       control_unit_1_regdstination, control_unit_1_regwrite;
  wire [1:0] control_unit_1_op1;
  wire [15:0] adder_1_out, adder_2_out, multiplexer_1_out, multiplexer_2_out, multiplexer_4_out,
       multiplexer_6_out, ram_1_data, register_1_q, registers_1_output, registers_1_output_2, rom_1_data,
       shifter_1_out, subtractor_1_out;
  wire [25:16] rom_1_data_2;

  Clock clock_1 (.out(clock_1_out));
  Register #(.width(16)) register_1 (
    .D(multiplexer_2_out), .en(clock_1_out), .Q(register_1_q), .clk(clock_1_out), .clr(in_9));
  Shifter #(.width(16)) shifter_1 (.in(rom_1_data), .\dist (in_4), .out(shifter_1_out));
  Adder #(.width(16)) adder_1 (.a(in_5), .b(register_1_q), .out(adder_1_out));  // open: cin, cout
  Subtractor #(.width(16)) subtractor_1 (.a(rom_1_data), .b(register_1_q), .out(subtractor_1_out));  // open: bin, bout
  Adder #(.width(16)) adder_2 (.a(shifter_1_out), .b(adder_1_out), .out(adder_2_out));  // open: cin, cout
  ROM #(.addrWidth(16), .dataWidth(32)) rom_1 (
    .addr(register_1_q), .data({out_15, rom_1_data_2, rom_1_data}));  // open: sel
  Multiplexer #(.width(16), .enable("false")) multiplexer_1 (
    .in0(adder_1_out), .in1(adder_2_out), .out(multiplexer_1_out), .sel(and_1_out));
  and and_1 (and_1_out, control_unit_1_branch, alu_1_out_9);
  Multiplexer #(.width(16), .enable("false")) multiplexer_2 (
    .in0(multiplexer_1_out), .in1(subtractor_1_out), .out(multiplexer_2_out), .sel(control_unit_1_jump));
  Multiplexer #(.width(3), .enable("false")) multiplexer_3 (
    .in0(rom_1_data_2[18:16]), .in1(rom_1_data[13:11]), .out(out_14), .sel(control_unit_1_regdstination));
  Control_Unit control_unit_1 (
    .Function(out_15), .Jump(control_unit_1_jump), .RegDstination(control_unit_1_regdstination),
    .ALUSource(control_unit_1_alusource), .MemtoReg(control_unit_1_memtoreg),
    .RegWrite(control_unit_1_regwrite), .Mem_Read(control_unit_1_mem_read),
    .Mem_Write(control_unit_1_mem_write), .Branch(control_unit_1_branch), .Op2(control_unit_1_op1[1]),
    .Op1(control_unit_1_op1[0]));
  Registers registers_1 (
    .Input(multiplexer_6_out), .RegWrite(control_unit_1_regwrite), .RD(out_14), .Output(registers_1_output),
    .Output_2(registers_1_output_2), .in_6(in_3), .RS(rom_1_data_2[23:21]), .RT(rom_1_data_2[18:16]));
  Multiplexer #(.width(16), .enable("false")) multiplexer_4 (
    .in0(registers_1_output_2), .in1(rom_1_data), .out(multiplexer_4_out), .sel(control_unit_1_alusource));
  Multiplexer #(.select(2), .width(4), .enable("false")) multiplexer_5 (
    .in0(in_1), .in1(in_2), .in2(rom_1_data[3:0]), .out(out_10), .sel(control_unit_1_op1));  // open: in3
  ALU alu_1 (
    .in_1(registers_1_output), .I(multiplexer_4_out), .in_8(rom_1_data[9:6]), .out_11(out_11), .in_6(out_10),
    .out_9(alu_1_out_9));  // open: in_3, in_4, in_5, in_7, out_10, out_12, out_13, out_14
  RAM #(.addrWidth(16), .dataWidth(16), .bus("separate")) ram_1 (
    .addr(out_11), .din(registers_1_output_2), .data(ram_1_data), .str(control_unit_1_mem_write),
    .clk(clock_1_out), .ld(control_unit_1_mem_read));  // open: sel, clr
  Multiplexer #(.width(16), .enable("false")) multiplexer_6 (
    .in0(out_11), .in1(ram_1_data), .out(multiplexer_6_out), .sel(control_unit_1_memtoreg));

  // Notes on the sheet:
  //   contents of rom_1 (hex, n*v repeats v):
  //   0 20430008 20620004 ac830003 8c000007 10030003
endmodule

module ALU (
  input  [15:0] in_1,
  input  [15:0] I,
  input  in_3,
  input  in_4,
  input  [15:0] in_5,
  input  [3:0] in_6,
  input  [15:0] in_7,
  input  [3:0] in_8,
  output out_9,
  output out_10,
  output [15:0] out_11,
  output out_12,
  output [15:0] out_13,
  output [15:0] out_14
);

  wire [15:0] adder_1_out, and_1_out, divider_1_out, multiplier_1_out, not_1_out, or_1_out, shifter_1_out,
       shifter_2_out, subtractor_1_out, xor_1_out;

  assign or_1_out = in_1 | I;  // OR_Gate or_1, 16 bits wide
  assign xor_1_out = in_1 ^ I;  // XOR_Gate xor_1, 16 bits wide
  assign not_1_out = ~in_1;  // NOT_Gate not_1, 16 bits wide
  Adder #(.width(16)) adder_1 (.a(in_1), .b(I), .out(adder_1_out), .cin(in_3), .cout(out_10));
  Subtractor #(.width(16)) subtractor_1 (.a(in_1), .b(I), .out(subtractor_1_out), .bin(in_4), .bout(out_12));
  Multiplier #(.width(16)) multiplier_1 (.a(in_1), .b(I), .out(multiplier_1_out), .cin(in_5), .cout(out_13));
  Divider #(.width(16)) divider_1 (.a(in_1), .b(I), .out(divider_1_out), .upper(in_7), .rem(out_14));
  Shifter #(.width(16)) shifter_1 (.in(I), .\dist (in_8), .out(shifter_1_out));
  Shifter #(.width(16), .shift("lr")) shifter_2 (.in(I), .\dist (in_8), .out(shifter_2_out));
  assign and_1_out = in_1 & I;  // AND_Gate and_1, 16 bits wide
  Multiplexer #(.select(4), .width(16), .enable("false")) multiplexer_1 (
    .in0(and_1_out), .in1(or_1_out), .in2(xor_1_out), .in3(not_1_out), .in4(adder_1_out),
    .in5(subtractor_1_out), .in6(multiplier_1_out), .in7(divider_1_out), .in8(shifter_1_out),
    .in9(shifter_2_out), .out({out_11[15:11], out_11[13], out_11[9:0]}), .sel(in_6));  // open: in10, in11, in12, in13, in14, in15
  nor nor_1 (out_9, out_11[0], out_11[1], out_11[2], out_11[3], out_11[4], out_11[5], out_11[6], out_11[7], out_11[8], out_11[9], out_11[13], out_11[11], out_11[12], out_11[13], out_11[14], out_11[15]);

  assign out_11[10] = out_11[13];
endmodule

module Registers (
  input  [15:0] Input,
  input  RegWrite,
  input  [2:0] RS,
  input  [2:0] RD,
  input  [2:0] RT,
  input  in_6,
  output [15:0] Output,
  output [15:0] Output_2
);

  wire and_1_out, and_2_out, and_3_out, and_4_out, and_5_out, and_6_out, and_7_out, and_8_out, clock_1_out,
       decoder_1_out0, decoder_1_out1, decoder_1_out2, decoder_1_out3, decoder_1_out4, decoder_1_out5,
       decoder_1_out6, decoder_1_out7;
  wire [15:0] register_1_q, register_2_q, register_3_q, register_4_q, register_5_q, register_6_q,
       register_7_q, register_8_q;

  Decoder #(.select(3), .enable("false")) decoder_1 (
    .out0(decoder_1_out0), .out1(decoder_1_out1), .out2(decoder_1_out2), .out3(decoder_1_out3),
    .out4(decoder_1_out4), .out5(decoder_1_out5), .out6(decoder_1_out6), .out7(decoder_1_out7), .sel(RD));
  and and_1 (and_1_out, RegWrite, decoder_1_out2);
  and and_2 (and_2_out, RegWrite, decoder_1_out0);
  and and_3 (and_3_out, RegWrite, decoder_1_out1);
  and and_4 (and_4_out, RegWrite, decoder_1_out3);
  and and_5 (and_5_out, RegWrite, decoder_1_out4);
  and and_6 (and_6_out, RegWrite, decoder_1_out5);
  and and_7 (and_7_out, RegWrite, decoder_1_out6);
  and and_8 (and_8_out, RegWrite, decoder_1_out7);
  Clock clock_1 (.out(clock_1_out));
  Register #(.width(16)) register_1 (.D(Input), .en(and_2_out), .Q(register_1_q), .clk(clock_1_out), .clr(in_6));
  Register #(.width(16)) register_2 (.D(Input), .en(and_3_out), .Q(register_2_q), .clk(clock_1_out), .clr(in_6));
  Register #(.width(16)) register_3 (.D(Input), .en(and_1_out), .Q(register_3_q), .clk(clock_1_out), .clr(in_6));
  Register #(.width(16)) register_4 (.D(Input), .en(and_4_out), .Q(register_4_q), .clk(clock_1_out), .clr(in_6));
  Register #(.width(16)) register_5 (.D(Input), .en(and_5_out), .Q(register_5_q), .clk(clock_1_out), .clr(in_6));
  Register #(.width(16)) register_6 (.D(Input), .en(and_6_out), .Q(register_6_q), .clk(clock_1_out), .clr(in_6));
  Register #(.width(16)) register_7 (.D(Input), .en(and_7_out), .Q(register_7_q), .clk(clock_1_out), .clr(in_6));
  Register #(.width(16)) register_8 (.D(Input), .en(and_8_out), .Q(register_8_q), .clk(clock_1_out), .clr(in_6));
  Multiplexer #(.select(3), .width(16), .enable("false")) multiplexer_1 (
    .in0(register_1_q), .in1(register_2_q), .in2(register_3_q), .in3(register_4_q), .in4(register_5_q),
    .in5(register_6_q), .in6(register_7_q), .in7(register_8_q), .out(Output), .sel(RS));
  Multiplexer #(.select(3), .width(16), .enable("false")) multiplexer_2 (
    .in0(register_1_q), .in1(register_2_q), .in2(register_3_q), .in3(register_4_q), .in4(register_5_q),
    .in5(register_6_q), .in6(register_7_q), .in7(register_8_q), .out(Output_2), .sel(RT));
endmodule

module Data_Memory (
  input  [15:0] Write_Data,
  input  [2:0] STA,
  input  [2:0] LDA,
  input  Mem_Read,
  input  in_5,
  input  MEM_READ_2,
  output [15:0] Data
);

  wire and_1_out, and_2_out, and_3_out, and_4_out, and_5_out, and_6_out, and_7_out, and_8_out, clock_1_out,
       decoder_1_out0, decoder_1_out1, decoder_1_out2, decoder_1_out3, decoder_1_out4, decoder_1_out5,
       decoder_1_out6, decoder_1_out7;
  wire [15:0] register_1_q, register_2_q, register_3_q, register_4_q, register_5_q, register_6_q,
       register_7_q, register_8_q;

  Decoder #(.select(3), .enable("false")) decoder_1 (
    .out0(decoder_1_out0), .out1(decoder_1_out1), .out2(decoder_1_out2), .out3(decoder_1_out3),
    .out4(decoder_1_out4), .out5(decoder_1_out5), .out6(decoder_1_out6), .out7(decoder_1_out7), .sel(STA));
  and and_1 (and_1_out, MEM_READ_2, decoder_1_out0);
  and and_2 (and_2_out, MEM_READ_2, decoder_1_out1);
  and and_3 (and_3_out, MEM_READ_2, decoder_1_out2);
  and and_4 (and_4_out, MEM_READ_2, decoder_1_out3);
  and and_5 (and_5_out, MEM_READ_2, decoder_1_out4);
  and and_6 (and_6_out, MEM_READ_2, decoder_1_out5);
  and and_7 (and_7_out, MEM_READ_2, decoder_1_out6);
  and and_8 (and_8_out, MEM_READ_2, decoder_1_out7);
  Clock clock_1 (.out(clock_1_out));
  Register #(.width(16)) register_1 (.D(Write_Data), .en(and_1_out), .Q(register_1_q), .clk(clock_1_out), .clr(in_5));
  Register #(.width(16)) register_2 (.D(Write_Data), .en(and_2_out), .Q(register_2_q), .clk(clock_1_out), .clr(in_5));
  Register #(.width(16)) register_3 (.D(Write_Data), .en(and_3_out), .Q(register_3_q), .clk(clock_1_out), .clr(in_5));
  Register #(.width(16)) register_4 (.D(Write_Data), .en(and_4_out), .Q(register_4_q), .clk(clock_1_out), .clr(in_5));
  Register #(.width(16)) register_5 (.D(Write_Data), .en(and_5_out), .Q(register_5_q), .clk(clock_1_out), .clr(in_5));
  Register #(.width(16)) register_6 (.D(Write_Data), .en(and_6_out), .Q(register_6_q), .clk(clock_1_out), .clr(in_5));
  Register #(.width(16)) register_7 (.D(Write_Data), .en(and_7_out), .Q(register_7_q), .clk(clock_1_out), .clr(in_5));
  Register #(.width(16)) register_8 (.D(Write_Data), .en(and_8_out), .Q(register_8_q), .clk(clock_1_out), .clr(in_5));
  Multiplexer #(.select(3), .width(16)) multiplexer_1 (
    .in0(register_1_q), .in1(register_2_q), .in2(register_3_q), .in3(register_4_q), .in4(register_5_q),
    .in5(register_6_q), .in6(register_7_q), .in7(register_8_q), .out(Data), .sel(LDA), .en(Mem_Read));
endmodule

module Control_Unit (
  input  [5:0] Function,
  output Jump,
  output RegDstination,
  output ALUSource,
  output MemtoReg,
  output RegWrite,
  output Mem_Read,
  output Mem_Write,
  output Branch,
  output Op2,
  output Op1
);

  wire addi_out;

  and R_Type (Op2, ~Function[5], ~Function[4], ~Function[3], ~Function[2], ~Function[1], ~Function[0]);  // AND_Gate
  and lw (Mem_Read, Function[5], ~Function[4], ~Function[3], ~Function[2], Function[1], Function[0]);  // AND_Gate
  and sw (Mem_Write, Function[5], ~Function[4], Function[3], ~Function[2], Function[1], Function[0]);  // AND_Gate
  and beq (Op1, ~Function[5], ~Function[4], ~Function[3], Function[2], ~Function[1], ~Function[0]);  // AND_Gate
  and u_jump (Jump, ~Function[5], ~Function[4], ~Function[3], ~Function[2], Function[1], ~Function[0]);  // AND_Gate
  and addi (addi_out, ~Function[5], ~Function[4], Function[3], ~Function[2], ~Function[1], ~Function[0]);  // AND_Gate
  or or_1 (ALUSource, Mem_Read, addi_out, Mem_Write);
  or or_2 (RegWrite, Op2, addi_out, Mem_Read);
  or or_3 (Branch, addi_out, Op1);

  assign MemtoReg = Mem_Read;
  assign RegDstination = Op2;
endmodule
