// Logisim project PROJECT 16BIT.circ as structural Verilog: 3 circuits, main circuit main
module main (
  input  in_1,
  input  in_2
);

  wire and_1_out;

  and and_1 (and_1_out, in_1, in_2);
endmodule

module ALU (
  input  [15:0] in_1,
  input  [15:0] in_2,
  input  in_3,
  input  in_4,
  input  in_5,
  input  in_6,
  input  [15:0] in_7,
  input  [3:0] operation,
  input  [15:0] in_9,
  input  [15:0] in_10,
  input  [15:0] in_11,
  input  [3:0] in_12,
  output out_13,
  output [15:0] out_14
);

  wire [15:0] adder_1_out, and_1_out, divider_1_out, multiplier_1_out, not_1_out, or_1_out, shifter_1_out,
       shifter_2_out, subtractor_1_out, xor_1_out;

  assign and_1_out = in_1 & in_2;  // AND_Gate and_1, 16 bits wide
  assign or_1_out = in_1 | in_2;  // OR_Gate or_1, 16 bits wide
  assign not_1_out = ~in_1;  // NOT_Gate not_1, 16 bits wide
  Subtractor #(.width(16)) subtractor_1 (.a(in_1), .b(in_2), .out(subtractor_1_out), .bin(in_5), .bout(in_6));
  Shifter #(.width(16)) shifter_1 (.in(in_2), .\dist (in_12), .out(shifter_1_out));
  Shifter #(.width(16), .shift("lr")) shifter_2 (.in(in_2), .\dist (in_12), .out(shifter_2_out));
  assign xor_1_out = in_1 ^ in_2;  // XOR_Gate xor_1, 16 bits wide
  Adder #(.width(16)) adder_1 (.a(in_1), .b(in_2), .out(adder_1_out), .cin(in_4), .cout(in_3));
  Multiplier #(.width(16)) multiplier_1 (.a(in_1), .b(in_2), .out(multiplier_1_out), .cin(in_7), .cout(in_9));
  Divider #(.width(16)) divider_1 (.a(in_1), .b(in_2), .out(divider_1_out), .upper(in_10), .rem(in_11));
  Multiplexer #(.select(4), .width(16), .enable("false")) multiplexer_1 (
    .in0(and_1_out), .in1(or_1_out), .in2(xor_1_out), .in3(not_1_out), .in4(adder_1_out),
    .in5(subtractor_1_out), .in6(multiplier_1_out), .in7(divider_1_out), .in8(shifter_1_out),
    .in9(shifter_2_out), .out(out_14), .sel(operation));  // open: in10, in11, in12, in13, in14, in15
  nor nor_1 (out_13, out_14[0], out_14[1], out_14[2], out_14[3], out_14[4], out_14[5], out_14[6], out_14[7], out_14[8], out_14[9], out_14[10], out_14[11], out_14[12], out_14[13], out_14[14], out_14[15]);

  // Notes on the sheet:
  //   data
  //   input-1
  //   data
  //   input-2
  //   result
endmodule

module Register (
  input  [15:0] in_1,
  input  [2:0] in_2,
  input  [2:0] in_3,
  input  [2:0] in_4,
  input  in_5,
  input  in_6,
  output [15:0] out_7,
  output [15:0] out_8
);

  wire and_1_out, and_2_out, and_3_out, and_4_out, and_5_out, and_6_out, and_7_out, and_8_out, clock_1_out,
       decoder_1_out0, decoder_1_out1, decoder_1_out2, decoder_1_out3, decoder_1_out4, decoder_1_out5,
       decoder_1_out6, decoder_1_out7;
  wire [15:0] register_1_q, register_2_q, register_3_q, register_4_q, register_5_q, register_6_q,
       register_7_q, register_8_q;

  Decoder #(.select(3), .enable("false")) decoder_1 (
    .out0(decoder_1_out0), .out1(decoder_1_out1), .out2(decoder_1_out2), .out3(decoder_1_out3),
    .out4(decoder_1_out4), .out5(decoder_1_out5), .out6(decoder_1_out6), .out7(decoder_1_out7), .sel(in_3));
  Clock clock_1 (.out(clock_1_out));
  and and_1 (and_1_out, in_6, decoder_1_out0);
  and and_2 (and_2_out, in_6, decoder_1_out1);
  and and_3 (and_3_out, in_6, decoder_1_out2);
  and and_4 (and_4_out, in_6, decoder_1_out3);
  and and_5 (and_5_out, in_6, decoder_1_out4);
  and and_6 (and_6_out, in_6, decoder_1_out5);
  and and_7 (and_7_out, in_6, decoder_1_out6);
  and and_8 (and_8_out, in_6, decoder_1_out7);
  Register_part #(.width(16)) register_1 (.D(in_1), .en(and_1_out), .Q(register_1_q), .clk(clock_1_out), .clr(in_5));
  Register_part #(.width(16)) register_2 (.D(in_1), .en(and_2_out), .Q(register_2_q), .clk(clock_1_out), .clr(in_5));
  Register_part #(.width(16)) register_3 (.D(in_1), .en(and_3_out), .Q(register_3_q), .clk(clock_1_out), .clr(in_5));
  Register_part #(.width(16)) register_4 (.D(in_1), .en(and_4_out), .Q(register_4_q), .clk(clock_1_out), .clr(in_5));
  Register_part #(.width(16)) register_5 (.D(in_1), .en(and_5_out), .Q(register_5_q), .clk(clock_1_out), .clr(in_5));
  Register_part #(.width(16)) register_6 (.D(in_1), .en(and_6_out), .Q(register_6_q), .clk(clock_1_out), .clr(in_5));
  Register_part #(.width(16)) register_7 (.D(in_1), .en(and_7_out), .Q(register_7_q), .clk(clock_1_out), .clr(in_5));
  Register_part #(.width(16)) register_8 (.D(in_1), .en(and_8_out), .Q(register_8_q), .clk(clock_1_out), .clr(in_5));
  Multiplexer #(.select(3), .width(16), .enable("false")) multiplexer_1 (
    .in0(register_1_q), .in1(register_2_q), .in2(register_3_q), .in3(register_4_q), .in4(register_5_q),
    .in5(register_6_q), .in6(register_7_q), .in7(register_8_q), .out(out_7), .sel(in_2));
  Multiplexer #(.select(3), .width(16), .enable("false")) multiplexer_2 (
    .in0(register_1_q), .in1(register_2_q), .in2(register_3_q), .in3(register_4_q), .in4(register_5_q),
    .in5(register_6_q), .in6(register_7_q), .in7(register_8_q), .out(out_8), .sel(in_4));
endmodule
