// Logisim project instruction-set.circ as structural Verilog: 6 circuits, main circuit main
module main (
  input  [7:0] in_1,
  input  Load,
  input  regwrite,
  input  [2:0] Rs,
  input  [2:0] Rd,
  input  [2:0] Rt,
  input  memWrite,
  input  Clear,
  input  [2:0] load_address,
  input  ALU_control,
  input  [2:0] store_address,
  input  MemtoReg,
  input  memRead,
  input  op1,
  input  clear_2,
  input  op2,
  input  op3,
  input  op4,
  input  op5,
  input  op6,
  input  [5:0] \function ,
  output [7:0] out_22,
  output [7:0] out_23,
  output [7:0] rs_2,
  output [7:0] rt_2,
  output out_26,
  output out_27,
  output [7:0] out_28,
  output [7:0] out_29
);

  Registers Register_System (
    .Write_Data(in_1), .Load(Load), .regwrite(regwrite), .rs(Rs), .rd(Rd), .rt(Rt), .clear(Clear),
    .rs_data(rs_2), .rt_data(rt_2));
  ALU alu_1 (
    .Rs(rs_2), .Rt(rt_2), .ALU_control(ALU_control), .in_4(op1), .in_5(op2), .in_6(op3), .in_7(op4),
    .in_8(op5), .in_9(op6), .func(\function ), .out(out_22), .c_out(out_26), .borrow_out(out_27),
    .mul_out(out_28), .remainder(out_29));
  Data_mem data_mem_1 (
    .Write_Data(out_22), .mem_write(memWrite), .load_address(load_address), .store_address(store_address),
    .mem_read(memRead), .clear(clear_2), .data(out_23));
  Multiplexer #(.width(8)) multiplexer_1 (.in0(out_23), .in1(out_22), .out(in_1), .sel(MemtoReg));  // open: en
endmodule

module Registers (
  input  [7:0] Write_Data,
  input  Load,
  input  regwrite,
  input  [2:0] rs,
  input  [2:0] rd,
  input  [2:0] rt,
  input  clear,
  output [7:0] rs_data,
  output [7:0] rt_data
);

  wire and_1_out, and_2_out, and_3_out, and_4_out, and_5_out, and_6_out, and_7_out, and_8_out, clock_out,
       decoder_1_out0, decoder_1_out1, decoder_1_out2, decoder_1_out3, decoder_1_out4, decoder_1_out5,
       decoder_1_out6, decoder_1_out7;
  wire [7:0] register_1_q, register_2_q, register_3_q, register_4_q, register_5_q, register_6_q,
       register_7_q, register_8_q;

  Decoder #(.select(3)) decoder_1 (
    .out0(decoder_1_out0), .out1(decoder_1_out1), .out2(decoder_1_out2), .out3(decoder_1_out3),
    .out4(decoder_1_out4), .out5(decoder_1_out5), .out6(decoder_1_out6), .out7(decoder_1_out7), .sel(rd),
    .en(regwrite));
  and and_1 (and_1_out, Load, decoder_1_out0);
  and and_2 (and_2_out, Load, decoder_1_out1);
  and and_3 (and_3_out, Load, decoder_1_out2);
  and and_4 (and_4_out, Load, decoder_1_out3);
  and and_5 (and_5_out, Load, decoder_1_out4);
  and and_6 (and_6_out, Load, decoder_1_out5);
  and and_7 (and_7_out, Load, decoder_1_out6);
  and and_8 (and_8_out, Load, decoder_1_out7);
  Register register_1 (.D(Write_Data), .en(and_1_out), .Q(register_1_q), .clk(clock_out), .clr(clear));
  Register register_2 (.D(Write_Data), .en(and_2_out), .Q(register_2_q), .clk(clock_out), .clr(clear));
  Register register_3 (.D(Write_Data), .en(and_3_out), .Q(register_3_q), .clk(clock_out), .clr(clear));
  Register register_4 (.D(Write_Data), .en(and_4_out), .Q(register_4_q), .clk(clock_out), .clr(clear));
  Register register_5 (.D(Write_Data), .en(and_5_out), .Q(register_5_q), .clk(clock_out), .clr(clear));
  Register register_6 (.D(Write_Data), .en(and_6_out), .Q(register_6_q), .clk(clock_out), .clr(clear));
  Register register_7 (.D(Write_Data), .en(and_7_out), .Q(register_7_q), .clk(clock_out), .clr(clear));
  Register register_8 (.D(Write_Data), .en(and_8_out), .Q(register_8_q), .clk(clock_out), .clr(clear));
  Clock clock (.out(clock_out));
  Multiplexer #(.select(3), .width(8), .enable("false")) multiplexer_1 (
    .in0(register_1_q), .in1(register_2_q), .in2(register_3_q), .in3(register_4_q), .in4(register_5_q),
    .in5(register_6_q), .in6(register_7_q), .in7(register_8_q), .out(rs_data), .sel(rs));
  Multiplexer #(.select(3), .width(8), .enable("false")) multiplexer_2 (
    .in0(register_1_q), .in1(register_2_q), .in2(register_3_q), .in3(register_4_q), .in4(register_5_q),
    .in5(register_6_q), .in6(register_7_q), .in7(register_8_q), .out(rt_data), .sel(rt));
endmodule

module ALU (
  input  [7:0] Rs,
  input  [7:0] Rt,
  input  ALU_control,
  input  in_4,
  input  in_5,
  input  in_6,
  input  in_7,
  input  in_8,
  input  in_9,
  input  [5:0] func,
  output [7:0] out,
  output c_out,
  output borrow_out,
  output [7:0] mul_out,
  output [7:0] remainder
);

  wire [2:0] control_unit_1_out_8;
  wire [7:0] adder_1_out, and_1_out, divider_1_out, multiplier_1_out, not_1_out, or_1_out, subtractor_1_out,
       xor_1_out;

  assign and_1_out = Rs & Rt;  // AND_Gate and_1, 8 bits wide
  assign or_1_out = Rs | Rt;  // OR_Gate or_1, 8 bits wide
  assign xor_1_out = Rs ^ Rt;  // XOR_Gate xor_1, 8 bits wide
  assign not_1_out = ~Rs;  // NOT_Gate not_1, 8 bits wide
  Adder adder_1 (.a(Rs), .b(Rt), .out(adder_1_out), .cout(c_out));  // open: cin
  Subtractor subtractor_1 (.a(Rs), .b(Rt), .out(subtractor_1_out), .bout(borrow_out));  // open: bin
  Multiplier multiplier_1 (.a(Rs), .b(Rt), .out(multiplier_1_out), .cout(mul_out));  // open: cin
  Divider divider_1 (.a(Rs), .b(Rt), .out(divider_1_out), .rem(remainder));  // open: upper
  Multiplexer #(.select(3), .width(8)) multiplexer_1 (
    .in0(and_1_out), .in1(or_1_out), .in2(not_1_out), .in3(xor_1_out), .in4(adder_1_out),
    .in5(subtractor_1_out), .in6(multiplier_1_out), .in7(divider_1_out), .out(out),
    .sel(control_unit_1_out_8), .en(ALU_control));
  control_unit control_unit_1 (
    .op1(in_4), .op2(in_5), .op3(in_6), .op4(in_7), .op5(in_8), .op6(in_9), .\function (func),
    .out_8(control_unit_1_out_8));
endmodule

// data mem
module Data_mem (
  input  [7:0] Write_Data,
  input  mem_write,
  input  [2:0] load_address,
  input  [2:0] store_address,
  input  mem_read,
  input  clear,
  output [7:0] data
);

  wire clock_out, decoder_1_out0, decoder_1_out1, decoder_1_out2, decoder_1_out3, decoder_1_out4,
       decoder_1_out5, decoder_1_out6, decoder_1_out7;
  wire [7:0] register_1_q, register_2_q, register_3_q, register_4_q, register_5_q, register_6_q,
       register_7_q, register_8_q;

  Decoder #(.select(3)) decoder_1 (
    .out0(decoder_1_out0), .out1(decoder_1_out1), .out2(decoder_1_out2), .out3(decoder_1_out3),
    .out4(decoder_1_out4), .out5(decoder_1_out5), .out6(decoder_1_out6), .out7(decoder_1_out7),
    .sel(store_address), .en(mem_write));
  Clock clock (.out(clock_out));
  Register register_1 (.D(Write_Data), .en(decoder_1_out0), .Q(register_1_q), .clk(clock_out), .clr(clear));
  Register register_2 (.D(Write_Data), .en(decoder_1_out1), .Q(register_2_q), .clk(clock_out), .clr(clear));
  Register register_3 (.D(Write_Data), .en(decoder_1_out2), .Q(register_3_q), .clk(clock_out), .clr(clear));
  Register register_4 (.D(Write_Data), .en(decoder_1_out3), .Q(register_4_q), .clk(clock_out), .clr(clear));
  Register register_5 (.D(Write_Data), .en(decoder_1_out4), .Q(register_5_q), .clk(clock_out), .clr(clear));
  Register register_6 (.D(Write_Data), .en(decoder_1_out5), .Q(register_6_q), .clk(clock_out), .clr(clear));
  Register register_7 (.D(Write_Data), .en(decoder_1_out6), .Q(register_7_q), .clk(clock_out), .clr(clear));
  Register register_8 (.D(Write_Data), .en(decoder_1_out7), .Q(register_8_q), .clk(clock_out), .clr(clear));
  Multiplexer #(.select(3), .width(8)) multiplexer_1 (
    .in0(register_1_q), .in1(register_2_q), .in2(register_3_q), .in3(register_4_q), .in4(register_5_q),
    .in5(register_6_q), .in6(register_7_q), .in7(register_8_q), .out(data), .sel(load_address), .en(mem_read));
endmodule

// alu control
module control_unit (
  input  op1,
  input  op2,
  input  op3,
  input  op4,
  input  op5,
  input  op6,
  input  [5:0] \function ,
  output [2:0] out_8
);

  wire nand_1_out;

  nand nand_1 (nand_1_out, op1, op2, op3, op4, op5, op6);
  and and_1 (out_8[2], nand_1_out, \function [2]);

  assign out_8[1:0] = \function [1:0];
endmodule

module Fetch (
  input  [7:0] in_1,
  input  in_2,
  input  [2:0] in_3,
  input  in_4,
  input  [3:0] in_5,
  input  in_6,
  output [7:0] out_7,
  output [7:0] out_8
);

  wire clock_1_out;
  wire [3:0] adder_1_out, register_1_q;
  wire [31:0] rom_1_data;

  Clock clock_1 (.out(clock_1_out));
  Adder #(.width(4)) adder_1 (.a(in_5), .b(register_1_q), .out(adder_1_out));  // open: cin, cout
  Register #(.width(4)) register_1 (.D(adder_1_out), .en(clock_1_out), .Q(register_1_q), .clk(clock_1_out), .clr(in_6));
  ROM #(.addrWidth(4), .dataWidth(32)) rom_1 (.addr(register_1_q), .data(rom_1_data));  // open: sel
  main main_1 (
    .in_1(in_1), .Load(in_2), .regwrite(in_2), .Rs(rom_1_data[23:21]), .Rd(in_3), .Rt(rom_1_data[18:16]),
    .ALU_control(in_4), .op1(rom_1_data[26]), .op2(rom_1_data[27]), .op3(rom_1_data[28]),
    .op4(rom_1_data[29]), .op5(rom_1_data[30]), .op6(rom_1_data[31]), .\function (rom_1_data[5:0]),
    .rs_2(out_7), .rt_2(out_8));  // open: memWrite, Clear, load_address, store_address, memRead, clear_2, MemtoReg, out_22, out_23, out_26, out_27, out_28, out_29

  // Notes on the sheet:
  //   contents of rom_1 (hex, n*v repeats v):
  //   222820 a11824 430820
endmodule
