// Logisim project project-1.circ as structural Verilog: 5 circuits, main circuit main
module main (
  input  in_1,
  input  Jump_Selector,
  input  in_3,
  input  in_4,
  input  Selector,
  input  WriteReg,
  input  Store,
  output out_8,
  output [15:0] out_9,
  output out_10
);

  wire CLK_out;
  wire [15:0] adder_1_out, bit_extender_1_out, multiplexer_1_out, multiplexer_2_out, multiplexer_3_out,
       ram_1_data, register_1_q, register_2_out_7, register_2_out_8;
  wire [31:0] rom_1_data;

  Register #(.width(16)) register_1 (.D(multiplexer_1_out), .Q(register_1_q), .clk(CLK_out));  // open: en, clr
  Adder #(.width(16)) adder_1 (.a(16'h1), .b(register_1_q), .out(adder_1_out));  // open: cin, cout
  Clock CLK (.out(CLK_out));
  Multiplexer #(.width(16), .enable("false")) multiplexer_1 (
    .in0(adder_1_out), .in1(bit_extender_1_out), .out(multiplexer_1_out), .sel(Jump_Selector));
  ROM #(.addrWidth(16), .dataWidth(32)) rom_1 (.addr(register_1_q), .data(rom_1_data));  // open: sel
  Bit_Extender #(.in_width(19)) bit_extender_1 (.in(rom_1_data[31:13]), .out(bit_extender_1_out));
  register register_2 (
    .Data(multiplexer_3_out), .out_7(register_2_out_7), .out_8(register_2_out_8), .RD(rom_1_data[6:4]),
    .WriteMem(WriteReg), .Clk(CLK_out), .RS(rom_1_data[9:7]), .RT(rom_1_data[12:10]));
  Multiplexer #(.width(16), .enable("false")) multiplexer_2 (
    .in0(register_2_out_8), .in1(bit_extender_1_out), .out(multiplexer_2_out), .sel(in_4));
  aluproject aluproject_1 (
    .Data1(register_2_out_7), .Data2(multiplexer_2_out), .Cin(in_1), .B_invert(in_3), .Cout(out_10),
    .Operation(rom_1_data[3:0]), .ZERO(out_8), .RESULT(out_9));
  RAM #(.addrWidth(16), .dataWidth(16), .bus("separate")) ram_1 (
    .addr(out_9), .data(ram_1_data), .str(Store));  // open: din, sel, clk, ld, clr
  Multiplexer #(.width(16), .enable("false")) multiplexer_3 (
    .in0(out_9), .in1(ram_1_data), .out(multiplexer_3_out), .sel(Selector));
endmodule

module aluproject (
  input  Cin,
  input  [15:0] Data1,
  input  [15:0] Data2,
  input  B_invert,
  input  [3:0] Operation,
  output ZERO,
  output Cout,
  output [15:0] RESULT
);

  wire [3:0] bit_extender_1_out, bit_extender_2_out;
  wire [15:0] adder_1_out, and_1_out, multiplexer_1_out, nor_1_out, not_1_out, or_1_out, shifter_1_out,
       shifter_2_out, xor_1_out;

  assign not_1_out = ~Data2;  // NOT_Gate not_1, 16 bits wide
  Multiplexer #(.width(16), .enable("false")) multiplexer_1 (
    .in0(Data2), .in1(not_1_out), .out(multiplexer_1_out), .sel(B_invert));
  Bit_Extender #(.in_width(16), .out_width(4)) bit_extender_1 (.in(Data2), .out(bit_extender_1_out));
  Bit_Extender #(.in_width(16), .out_width(4)) bit_extender_2 (.in(Data2), .out(bit_extender_2_out));
  Shifter #(.width(16), .shift("ar")) shifter_1 (.in(Data1), .\dist (bit_extender_1_out), .out(shifter_1_out));
  Shifter #(.width(16)) shifter_2 (.in(Data1), .\dist (bit_extender_2_out), .out(shifter_2_out));
  Adder #(.width(16)) adder_1 (.a(Data1), .b(multiplexer_1_out), .out(adder_1_out), .cin(Cin), .cout(Cout));
  assign and_1_out = Data1 & Data2;  // AND_Gate and_1, 16 bits wide
  assign or_1_out = Data1 | Data2;  // OR_Gate or_1, 16 bits wide
  assign xor_1_out = Data1 ^ Data2;  // XOR_Gate xor_1, 16 bits wide
  assign nor_1_out = ~(Data1 | Data2);  // NOR_Gate nor_1, 16 bits wide
  Multiplexer #(.select(4), .width(16), .enable("false")) multiplexer_2 (
    .in0(adder_1_out), .in1(adder_1_out), .in2(and_1_out), .in3(or_1_out), .in4(xor_1_out), .in5(nor_1_out),
    .in6(shifter_2_out), .in7(shifter_1_out), .in8(adder_1_out), .in9(adder_1_out), .in10(adder_1_out),
    .in11(Data2), .out(RESULT), .sel(Operation));  // open: in12, in13, in14, in15
  nor nor_2 (ZERO, RESULT[0], RESULT[1], RESULT[2], RESULT[3], RESULT[4], RESULT[5], RESULT[6], RESULT[7], RESULT[8], RESULT[9], RESULT[10], RESULT[11], RESULT[12], RESULT[13], RESULT[14], RESULT[15]);
endmodule

module register (
  input  [15:0] Data,
  input  [2:0] RS,
  input  [2:0] RD,
  input  [2:0] RT,
  input  WriteMem,
  input  Clk,
  output [15:0] out_7,
  output [15:0] out_8
);

  wire and_2_out, and_3_out, and_4_out, and_5_out, and_6_out, and_7_out, and_8_out, decoder_1_out0,
       decoder_1_out1, decoder_1_out2, decoder_1_out3, decoder_1_out4, decoder_1_out5, decoder_1_out6,
       decoder_1_out7;
  wire [15:0] register_1_q, register_2_q, register_3_q, register_4_q, register_5_q, register_6_q,
       register_7_q, register_8_q;

  Decoder #(.select(3), .enable("false")) decoder_1 (
    .out0(decoder_1_out0), .out1(decoder_1_out1), .out2(decoder_1_out2), .out3(decoder_1_out3),
    .out4(decoder_1_out4), .out5(decoder_1_out5), .out6(decoder_1_out6), .out7(decoder_1_out7), .sel(RD));
  // AND_Gate and_1 has open pins: in0=WriteMem, in1=decoder_1_out0, out=open
  and and_2 (and_2_out, WriteMem, decoder_1_out1);
  and and_3 (and_3_out, WriteMem, decoder_1_out2);
  and and_4 (and_4_out, WriteMem, decoder_1_out3);
  and and_5 (and_5_out, WriteMem, decoder_1_out4);
  and and_6 (and_6_out, WriteMem, decoder_1_out5);
  and and_7 (and_7_out, WriteMem, decoder_1_out6);
  and and_8 (and_8_out, WriteMem, decoder_1_out7);
  Register #(.width(16)) register_1 (.Q(register_1_q), .clk(Clk));  // open: D, en, clr
  Register #(.width(16)) register_2 (.D(Data), .en(and_2_out), .Q(register_2_q), .clk(Clk));  // open: clr
  Register #(.width(16)) register_3 (.D(Data), .en(and_3_out), .Q(register_3_q), .clk(Clk));  // open: clr
  Register #(.width(16)) register_4 (.D(Data), .en(and_4_out), .Q(register_4_q), .clk(Clk));  // open: clr
  Register #(.width(16)) register_5 (.D(Data), .en(and_5_out), .Q(register_5_q), .clk(Clk));  // open: clr
  Register #(.width(16)) register_6 (.D(Data), .en(and_6_out), .Q(register_6_q), .clk(Clk));  // open: clr
  Register #(.width(16)) register_7 (.D(Data), .en(and_7_out), .Q(register_7_q), .clk(Clk));  // open: clr
  Register #(.width(16)) register_8 (.D(Data), .en(and_8_out), .Q(register_8_q), .clk(Clk));  // open: clr
  Multiplexer #(.select(3), .width(16), .enable("false")) multiplexer_1 (
    .in0(register_1_q), .in1(register_2_q), .in2(register_3_q), .in3(register_4_q), .in4(register_5_q),
    .in5(register_6_q), .in6(register_7_q), .in7(register_8_q), .out(out_7), .sel(RS));
  Multiplexer #(.select(3), .width(16), .enable("false")) multiplexer_2 (
    .in0(register_1_q), .in1(register_2_q), .in2(register_3_q), .in3(register_4_q), .in4(register_5_q),
    .in5(register_6_q), .in6(register_7_q), .in7(register_8_q), .out(out_8), .sel(RT));
endmodule

module control_unit (
  input  [2:0] Opcode,
  output MemToReg,
  output reg_control,
  output AluSrc,
  output AluOp0,
  output AluOp1,
  output regWrite,
  output Brunch,
  output mem_read,
  output Jump,
  output mem_write
);

  wire and_5_out, and_6_out, not_1_out, not_3_out;

  and and_1 (mem_write, Opcode[0], Opcode[1]);
  and and_2 (Jump, Opcode[0], Opcode[2]);
  and and_3 (mem_read, Opcode[1], not_1_out);
  and and_4 (Brunch, Opcode[2], not_1_out);
  not not_1 (not_1_out, Opcode[0]);
  not not_2 (MemToReg, Opcode[1]);
  not not_3 (not_3_out, Opcode[2]);
  and and_5 (and_5_out, MemToReg, not_3_out);
  and and_6 (and_6_out, Opcode[1], not_1_out);
  or or_1 (AluOp0, Opcode[0], Opcode[1]);
  or or_2 (regWrite, and_6_out, and_5_out);

  assign AluOp1 = Opcode[2];
  assign AluSrc = AluOp0;
  assign reg_control = AluOp0;
endmodule

module alucontrol (
  input  Aluop0,
  input  AluOp1,
  input  [2:0] \function 
);

  wire decoder_1_out0, decoder_1_out1, decoder_1_out4, decoder_1_out5, decoder_1_out7;
  wire [3:1] or_2_out;

  Decoder #(.select(5)) decoder_1 (
    .out0(decoder_1_out0), .out1(decoder_1_out1), .out4(decoder_1_out4), .out5(decoder_1_out5),
    .out7(decoder_1_out7), .sel({AluOp1, Aluop0, \function }));  // open: out2, out3, out6, out8, out9, out10, out11, out12, out13, out14, out15, out16, out17, out18, out19, out20, out21, out22, out23, out24, out25, out26, out27, out28, out29, out30, out31, en
  or or_1 (or_2_out[3], decoder_1_out4, decoder_1_out5);
  or or_2 (or_2_out[1], decoder_1_out0, decoder_1_out1, decoder_1_out7);
endmodule
